# Fritzing sketch Proyecto_final_embebidos3 (saved by Fritzing 0.9.9b)
breadboards: 2

parts:
  U5 = POT [package=pot_mammoth]
  R3 = Resistor [tolerance=±5% power=0.25 resistance=220 package=THT]
  U8 = ESP32S-HiLetgo [part_number=ESP32S-HiLetgo]
  M2 = ac light dimmer 3terminal
  Power_plug2 = Power plug
  T1 = LM35 Temperature Sensor [package="TO92 [THT]"]
  LED1 = LEDs [package=led10mm]
  LCD1 = LCD screen
  U10 = POT [package=pot_alpha_rv16af-20]
  R6 = Resistor [tolerance=±5% power=0.25 resistance=220 package=THT]

nets:
  N1: U5.S, M2.GND
  N2: U5.A, U8.GPIO0
  N3: U5.E, T1.+Vs, U10.E, R6.Pin_0
  N4: R3.Pin_0, U8.GPIO12, T1.Vout
  N5: R3.Pin_1, T1.GND, LCD1.LED-
  VCC: U8.3.3, M2.VCC, Power_plug2.VCC
  GND: U8.GND, M2.IN, Power_plug2.GND
  N6: U8.GPIO15, LCD1.DB7
  N7: U8.GPIO2, LCD1.DB6
  N8: U8.GPIO4, LCD1.DB5
  N9: U8.GPIO16, M2.PWM
  N10: U8.GPIO17, M2.Z-C
  N11: U8.GPIO5, LCD1.DB4
  N12: U8.GPIO18, LCD1.E
  N13: U8.GPIO19, LCD1.RS
  N14: M2.OUT, LED1.C
  N15: M2.N, LED1.A
  N16: LCD1.V0, U10.S
  N17: LCD1.LED+, R6.Pin_1

custom parts:
  ESP32S-HiLetgo: HiLetgo ESP-WROOM-32 ESP32 ESP-32S Development Board 2.4GHz Dual-Mode WiFi + Bluetooth Dual Cores Microcontroller The ESP32 integrated with Antenna switches, RF Balun, power amplifiers, low-noise amplifiers, filters, and management modules, and the entire solution occupies the least area of PCB. 2.4 GHz Wi-Fi plus Bluetooth dual-mode chip, with TSMC Ultra-low power consumption 40nm technology,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
  ac light dimmer 3terminal: ac light dimmer module 3 output terminals.
  LEDs: LEDs Standard schematic elements and footprints for 5mm, 3mm, 1206, and 0603 sized LEDs. 5mm - Spark Fun Electronics SKU : COM-00529 (and others)
