# Fritzing sketch Proyecto_final_embebidos_2 (saved by Fritzing 0.9.9b)
breadboards: 2

parts:
  U1 = ESP32S-HiLetgo [part_number=ESP32S-HiLetgo]
  U2 = POT [package=pot_alpha_rv16af-20]
  LCD1 = LCD screen
  R1 = Resistor [tolerance=±5% resistance=220 package="0805 [SMD]"]
  R2 = Resistor [tolerance=±5% resistance=220 package="0805 [SMD]"]
  R3 = Resistor [tolerance=±5% resistance=220 package="0805 [SMD]"]
  R4 = Resistor [tolerance=±5% resistance=220 package="0805 [SMD]"]
  LED1 = smd LED [color="Blue (525nm)" package="1206 [SMD]"]
  LED2 = smd LED [color="Green (560nm)" package="1206 [SMD]"]
  LED3 = smd LED [color="Red (633nm)" package="1206 [SMD]"]
  Power_plug1 = Power plug  # not connected
  e-radionica1 = TCS230 Color Sensor [part_number=101209]

nets (from the breadboard view):
  N1: U1.3.3, e-radionica1.Vcc
  N2: U1.GPIO34, LED3.anode
  N3: U1.GPIO35, LED1.anode
  N4: U1.GPIO32, LED2.anode
  GND: U1.GND, e-radionica1.Gnd
  N5: U1.GPIO15, LCD1.DB7
  N6: U1.GPIO2, LCD1.DB6
  N7: U1.GPIO0, LCD1.DB5
  N8: U1.GPIO4, LCD1.DB4
  N9: U1.GPIO16, LCD1.E
  N10: U1.GPIO17, LCD1.RS
  N11: U1.GPIO5, e-radionica1.Out
  N12: U1.GPIO18, e-radionica1.S3
  N13: U1.GPIO19, e-radionica1.S1
  N14: U1.GPIO21, e-radionica1.S0
  N15: U1.GPIO3, e-radionica1.S2
  N16: U2.S, LCD1.V0
  N17: U2.E, R4.Pin_1
  N18: LCD1.R/W, R1.Pin_1, R2.Pin_1, R3.Pin_1
  N19: LCD1.LED+, R4.Pin_0
  N20: R1.Pin_0, LED1.cathode
  N21: R2.Pin_0, LED2.cathode
  N22: R3.Pin_0, LED3.cathode

notes:
  TCS230
  RGB light/color sensor
  +5V
  GND

custom parts:
  ESP32S-HiLetgo: HiLetgo ESP-WROOM-32 ESP32 ESP-32S Development Board 2.4GHz Dual-Mode WiFi + Bluetooth Dual Cores Microcontroller The ESP32 integrated with Antenna switches, RF Balun, power amplifiers, low-noise amplifiers, filters, and management modules, and the entire solution occupies the least area of PCB. 2.4 GHz Wi-Fi plus Bluetooth dual-mode chip, with TSMC Ultra-low power consumption 40nm technology,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
  TCS230 Color Sensor: TCS230
