# Fritzing sketch servos (saved by Fritzing 0.9.9b)
breadboards: 1

parts:
  M2 = Dagu DGServo 9g (Top view) [part_number=RS001B]
  M3 = Dagu DGServo 9g (Top view) [part_number=RS001B]
  U1 = ESP32S-HiLetgo [part_number=ESP32S-HiLetgo]
  U2 = TRANSISTOR_NPN_2 [package=to-92]
  U3 = TRANSISTOR_NPN_2 [package=to-92]
  U4 = Sharp PC817 [package=THT]
  U5 = Sharp PC817 [package=THT]
  U6 = Sharp PC817 [package=THT]
  M4 = Stepper Motor - Bipolar
  DRV_1 = DRV 8825 Stepper Motor Carrier, High Current [part_number="DRV 8825"]
  R1 = Resistor [tolerance=±5% resistance=220 package="2512 [SMD]"]
  R2 = Resistor [tolerance=±5% resistance=220 package="2512 [SMD]"]
  R3 = Resistor [tolerance=±5% resistance=220 package="2512 [SMD]"]
  R4 = Resistor [tolerance=±5% resistance=220 package="2512 [SMD]"]
  R6 = Resistor [tolerance=±5% resistance=220 package="0603 [SMD]"]

nets:
  N1: M2.gnd, U3.C
  VCC: M2.vcc, M3.vcc, U2.E, U3.E
  N2: M2.pulse, M3.pulse, U1.GPIO22
  N3: M3.gnd, U2.C
  N4: U1.GND, U4.Pin_2, U5.Pin_2, U6.Pin_2
  N5: U1.GPIO2, R6.Pin_0
  N6: U1.GPIO18, R1.Pin_0
  N7: U1.GPIO19, R2.Pin_0
  N8: U2.B, R4.Pin_1
  N9: U3.B, R3.Pin_1
  N10: U4.Pin_1, R1.Pin_1
  N11: U4.Pin_3, R4.Pin_0
  N12: U5.Pin_1, R6.Pin_1
  N13: U5.Pin_3, DRV_1.ENABLE
  N14: U6.Pin_1, R2.Pin_1
  N15: U6.Pin_3, R3.Pin_0
  N16: M4.A, DRV_1.OUT_1A
  N17: M4.C, DRV_1.OUT_1B
  N18: M4.B, DRV_1.OUT_2A
  N19: M4.D, DRV_1.OUT_2B

custom parts:
  ESP32S-HiLetgo: HiLetgo ESP-WROOM-32 ESP32 ESP-32S Development Board 2.4GHz Dual-Mode WiFi + Bluetooth Dual Cores Microcontroller The ESP32 integrated with Antenna switches, RF Balun, power amplifiers, low-noise amplifiers, filters, and management modules, and the entire solution occupies the least area of PCB. 2.4 GHz Wi-Fi plus Bluetooth dual-mode chip, with TSMC Ultra-low power consumption 40nm technology,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
